// Logisim project single_cycle_CPU.circ as structural Verilog: 8 circuits, main circuit main
module main (
);


  // Notes on the sheet:
  //   Please refer to the Processor Circuit...
endmodule

module Adder (
  input  [31:0] in_1,
  input  [31:0] in_2,
  output [31:0] out_3,
  output out_4
);

  Adder_part #(.width(32)) adder_1 (.a(in_1), .b(in_2), .out(out_3), .cout(out_4));  // open: cin

  // Notes on the sheet:
  //   ADDER__CKT
endmodule

module Subtractor (
  input  [31:0] in_1,
  input  [31:0] in_2,
  output [31:0] out_3,
  output out_4
);

  Subtractor_part #(.width(32)) subtractor_1 (.a(in_1), .b(in_2), .out(out_3), .bout(out_4));  // open: bin
endmodule

module Control_Unit (
  input  [5:0] Opcode,
  output Jump,
  output ALURequired,
  output RegDest,
  output Branch,
  output MemWrite,
  output MemRead,
  output MemToReg,
  output RegWrite,
  output ALUSrc,
  output R_type,
  output [1:0] ALUOp
);

  wire ADDI_out, ANDI_out, BEQ_out, BNE_out, ORI_out, SLTI_out, XORI_out;

  and u_R_type (R_type, ~Opcode[5], ~Opcode[4], ~Opcode[3], ~Opcode[2], ~Opcode[1], ~Opcode[0]);  // AND_Gate
  and LW (MemRead, Opcode[5], ~Opcode[4], ~Opcode[3], ~Opcode[2], Opcode[1], Opcode[0]);  // AND_Gate
  and SW (MemWrite, Opcode[5], ~Opcode[4], Opcode[3], ~Opcode[2], Opcode[1], Opcode[0]);  // AND_Gate
  and BEQ (BEQ_out, ~Opcode[5], ~Opcode[4], ~Opcode[3], Opcode[2], ~Opcode[1], ~Opcode[0]);  // AND_Gate
  and ADDI (ADDI_out, ~Opcode[5], ~Opcode[4], Opcode[3], ~Opcode[2], ~Opcode[1], ~Opcode[0]);  // AND_Gate
  and SLTI (SLTI_out, ~Opcode[5], ~Opcode[4], Opcode[3], ~Opcode[2], Opcode[1], ~Opcode[0]);  // AND_Gate
  and ANDI (ANDI_out, ~Opcode[5], ~Opcode[4], Opcode[3], Opcode[2], ~Opcode[1], ~Opcode[0]);  // AND_Gate
  and ORI (ORI_out, ~Opcode[5], ~Opcode[4], Opcode[3], Opcode[2], ~Opcode[1], Opcode[0]);  // AND_Gate
  and XORI (XORI_out, ~Opcode[5], ~Opcode[4], Opcode[3], Opcode[2], Opcode[1], ~Opcode[0]);  // AND_Gate
  ROM #(.addrWidth(6), .dataWidth(2)) rom_1 (.addr(Opcode), .data(ALUOp));  // open: sel
  and J (Jump, ~Opcode[5], ~Opcode[4], ~Opcode[3], ~Opcode[2], Opcode[1], ~Opcode[0]);  // AND_Gate
  and BNE (BNE_out, ~Opcode[5], ~Opcode[4], ~Opcode[3], Opcode[2], ~Opcode[1], Opcode[0]);  // AND_Gate
  not not_1 (ALURequired, Jump);
  or or_1 (Branch, BNE_out, BEQ_out);
  or u_RegWrite (RegWrite, XORI_out, ORI_out, ANDI_out, SLTI_out, ADDI_out, MemRead, R_type);
  nor nor_1 (ALUSrc, BNE_out, BEQ_out, R_type);

  assign MemToReg = MemRead;
  assign RegDest = R_type;

  // Notes on the sheet:
  //   contents of rom_1 (hex, n*v repeats v):
  //   2 0 0 0 1 1 4*0 3 0 3 3 3
endmodule

module ALU_CTRL (
  input  [5:0] OPCODE,
  input  [5:0] Funct,
  input  R_type,
  output [3:0] ALU_CONTROL
);

  wire ADD_out, or_2_out;
  wire [3:0] multiplexer_1_out;
  wire [8:0] multiplexer_2_out;

  Multiplexer #(.width(4), .enable("false")) multiplexer_1 (
    .in0(4'b0001), .in1(Funct[3:0]), .out(multiplexer_1_out), .sel(R_type));
  Multiplexer #(.enable("false")) multiplexer_2 (.in0(ADD_out), .in1(1'b0), .out(multiplexer_2_out[0]), .sel(or_2_out));
  and ADD (ADD_out, ~multiplexer_1_out[3], ~multiplexer_1_out[2], ~multiplexer_1_out[1], ~multiplexer_1_out[0]);  // AND_Gate
  and SUB (multiplexer_2_out[1], ~multiplexer_1_out[3], ~multiplexer_1_out[2], multiplexer_1_out[1], ~multiplexer_1_out[0]);  // AND_Gate
  and AND (multiplexer_2_out[2], ~multiplexer_1_out[3], multiplexer_1_out[2], ~multiplexer_1_out[1], ~multiplexer_1_out[0]);  // AND_Gate
  ROM #(.addrWidth(9), .dataWidth(4)) rom_1 (.addr(multiplexer_2_out), .data(ALU_CONTROL));  // open: sel
  and OR (multiplexer_2_out[3], ~multiplexer_1_out[3], multiplexer_1_out[2], ~multiplexer_1_out[1], multiplexer_1_out[0]);  // AND_Gate
  and XOR (multiplexer_2_out[4], ~multiplexer_1_out[3], multiplexer_1_out[2], multiplexer_1_out[1], ~multiplexer_1_out[0]);  // AND_Gate
  and SLT (multiplexer_2_out[5], multiplexer_1_out[3], ~multiplexer_1_out[2], multiplexer_1_out[1], ~multiplexer_1_out[0]);  // AND_Gate
  or or_2 (or_2_out, multiplexer_2_out[6], multiplexer_2_out[7], multiplexer_2_out[8]);
  Comparator #(.width(6)) comparator_1 (.a(OPCODE), .b(6'b000100), .eq(multiplexer_2_out[6]));  // open: gt, lt
  Comparator #(.width(6)) comparator_2 (.a(OPCODE), .b(6'b000101), .eq(multiplexer_2_out[7]));  // open: gt, lt
  Comparator #(.width(6)) comparator_3 (.a(OPCODE), .b(6'b001000), .eq(multiplexer_2_out[8]));  // open: gt, lt

  // Notes on the sheet:
  //   contents of rom_1 (hex, n*v repeats v):
  //   0 0 1 0 5 0 0 0 4 7*0 3 15*0 2 31*0 8 63*0 9
  //   BEQ
  //   BNE
  //   ADDI
endmodule

module ALU (
  input  [3:0] ALU_Control,
  input  [31:0] in_2,
  input  [31:0] in_3,
  output out_4,
  output Branch,
  output [31:0] out_6
);

  wire adder_1_out_4, comparator_1_eq, comparator_1_lt, comparator_2_eq, comparator_3_eq, comparator_4_eq,
       multiplexer_5_out, not_1_out, subtractor_1_out_4;
  wire [31:0] adder_1_out_3, and_1_out, multiplexer_1_out, multiplexer_2_out, multiplexer_3_out, or_1_out,
       subtractor_1_out_3, xor_1_out;

  Adder adder_1 (.out_3(adder_1_out_3), .in_1(in_2), .in_2(in_3), .out_4(adder_1_out_4));
  Subtractor subtractor_1 (.out_3(subtractor_1_out_3), .out_4(subtractor_1_out_4), .in_1(in_2), .in_2(in_3));
  Comparator #(.width(32)) comparator_1 (.a(in_2), .b(in_3), .eq(comparator_1_eq), .lt(comparator_1_lt));  // open: gt
  not not_1 (not_1_out, comparator_1_eq);
  assign xor_1_out = in_2 ^ in_3;  // XOR_Gate xor_1, 32 bits wide
  assign or_1_out = in_2 | in_3;  // OR_Gate or_1, 32 bits wide
  assign and_1_out = in_2 & in_3;  // AND_Gate and_1, 32 bits wide
  Multiplexer #(.width(32), .enable("false")) multiplexer_1 (
    .in0({32{1'b0}}), .in1(32'h1), .out(multiplexer_1_out), .sel(comparator_1_lt));
  Multiplexer #(.width(32), .enable("false")) multiplexer_2 (
    .in0({32{1'b0}}), .in1(32'h1), .out(multiplexer_2_out), .sel(comparator_1_eq));
  Multiplexer #(.width(32), .enable("false")) multiplexer_3 (
    .in0({32{1'b0}}), .in1(32'h1), .out(multiplexer_3_out), .sel(not_1_out));
  Multiplexer #(.select(4), .width(32), .enable("false")) multiplexer_4 (
    .in0(adder_1_out_3), .in1(subtractor_1_out_3), .in2(multiplexer_1_out), .in3(xor_1_out), .in4(or_1_out),
    .in5(and_1_out), .in8(multiplexer_2_out), .in9(multiplexer_3_out), .out(out_6), .sel(ALU_Control));  // open: in6, in7, in10, in11, in12, in13, in14, in15
  Multiplexer #(.enable("false")) multiplexer_5 (
    .in0(adder_1_out_4), .in1(subtractor_1_out_4), .out(multiplexer_5_out), .sel(ALU_Control[0]));
  Comparator #(.width(3), .mode("unsigned")) comparator_2 (
    .a(ALU_Control[3:1]), .b(3'b000), .eq(comparator_2_eq));  // open: gt, lt
  Comparator #(.width(1), .mode("unsigned")) comparator_3 (
    .a(ALU_Control[3]), .b(1'b1), .eq(comparator_3_eq));  // open: gt, lt
  Comparator #(.width(32), .mode("unsigned")) comparator_4 (
    .a(32'h1), .b(out_6), .eq(comparator_4_eq));  // open: gt, lt
  and and_2 (out_4, comparator_2_eq, multiplexer_5_out);
  and and_3 (Branch, comparator_3_eq, comparator_4_eq);

  // Notes on the sheet:
  //   A
  //   B
  //   , ADDI
  //   ADD
  //   SUB
  //   , SUBI
  //   XOR
  //   , XORI
  //   OR
  //   , ORI
  //   , ANDI
  //   AND
  //   SLT
  //   BEQ
  //   BNE
  //   OVERFLOW
  //   UNDERFLOW
  //   Output
  //   OVERFLOW / UNDERFLOW
endmodule

module Register_file (
  input  [4:0] ReadReg1,
  input  [4:0] ReadReg2,
  input  [4:0] WriteReg,
  input  RegWrite,
  input  [31:0] WriteData,
  input  Clk,
  input  Reset,
  output [31:0] ReadData1,
  output [31:0] ReadData2
);

  wire decoder_1_out0, decoder_1_out1, decoder_2_out0, decoder_2_out1, decoder_2_out2, decoder_2_out3,
       decoder_3_out0, decoder_3_out1, decoder_3_out2, decoder_3_out3, decoder_4_out0, decoder_4_out1,
       decoder_4_out2, decoder_4_out3, decoder_5_out0, decoder_5_out1, decoder_5_out2, decoder_5_out3,
       decoder_6_out0, decoder_6_out1, decoder_6_out2, decoder_6_out3, decoder_7_out0, decoder_7_out1,
       decoder_7_out2, decoder_7_out3, decoder_8_out0, decoder_8_out1, decoder_8_out2, decoder_8_out3,
       decoder_9_out0, decoder_9_out1, decoder_9_out2, decoder_9_out3, decoder_10_out0, decoder_10_out1,
       decoder_10_out2, decoder_10_out3, decoder_11_out0, decoder_11_out1, decoder_11_out2, decoder_11_out3;
  wire [31:0] multiplexer_1_out, multiplexer_2_out, multiplexer_3_out, multiplexer_4_out, multiplexer_5_out,
       multiplexer_6_out, multiplexer_7_out, multiplexer_8_out, multiplexer_9_out, multiplexer_10_out,
       multiplexer_13_out, multiplexer_14_out, multiplexer_15_out, multiplexer_16_out, multiplexer_17_out,
       multiplexer_18_out, multiplexer_19_out, multiplexer_20_out, multiplexer_21_out, multiplexer_22_out,
       register_1_q, register_2_q, register_3_q, register_4_q, register_5_q, register_6_q, register_7_q,
       register_8_q, register_9_q, register_10_q, register_11_q, register_12_q, register_13_q, register_14_q,
       register_15_q, register_16_q, register_17_q, register_18_q, register_19_q, register_20_q,
       register_21_q, register_22_q, register_23_q, register_24_q, register_25_q, register_26_q,
       register_27_q, register_28_q, register_29_q, register_30_q, register_31_q;

  // Probe on WriteReg
  Decoder #(.disabled(0)) decoder_1 (.out0(decoder_1_out0), .out1(decoder_1_out1), .sel(WriteReg[4]), .en(RegWrite));
  Decoder #(.select(2), .disabled(0)) decoder_2 (
    .out0(decoder_2_out0), .out1(decoder_2_out1), .out2(decoder_2_out2), .out3(decoder_2_out3),
    .sel(WriteReg[3:2]), .en(decoder_1_out0));
  Decoder #(.select(2), .disabled(0)) decoder_3 (
    .out0(decoder_3_out0), .out1(decoder_3_out1), .out2(decoder_3_out2), .out3(decoder_3_out3),
    .sel(WriteReg[1:0]), .en(decoder_2_out0));
  Decoder #(.select(2), .disabled(0)) decoder_4 (
    .out0(decoder_4_out0), .out1(decoder_4_out1), .out2(decoder_4_out2), .out3(decoder_4_out3),
    .sel(WriteReg[1:0]), .en(decoder_2_out1));
  Decoder #(.select(2), .disabled(0)) decoder_5 (
    .out0(decoder_5_out0), .out1(decoder_5_out1), .out2(decoder_5_out2), .out3(decoder_5_out3),
    .sel(WriteReg[1:0]), .en(decoder_2_out2));
  Decoder #(.select(2), .disabled(0)) decoder_6 (
    .out0(decoder_6_out0), .out1(decoder_6_out1), .out2(decoder_6_out2), .out3(decoder_6_out3),
    .sel(WriteReg[1:0]), .en(decoder_2_out3));
  Register #(.width(32)) register_1 (.D(WriteData), .en(decoder_3_out1), .Q(register_1_q), .clk(Clk), .clr(Reset));
  Register #(.width(32)) register_2 (.D(WriteData), .en(decoder_3_out2), .Q(register_2_q), .clk(Clk), .clr(Reset));
  Register #(.width(32)) register_3 (.D(WriteData), .en(decoder_3_out3), .Q(register_3_q), .clk(Clk), .clr(Reset));
  Register #(.width(32)) register_4 (.D(WriteData), .en(decoder_4_out0), .Q(register_4_q), .clk(Clk), .clr(Reset));
  Register #(.width(32)) register_5 (.D(WriteData), .en(decoder_4_out1), .Q(register_5_q), .clk(Clk), .clr(Reset));
  Register #(.width(32)) register_6 (.D(WriteData), .en(decoder_4_out2), .Q(register_6_q), .clk(Clk), .clr(Reset));
  Register #(.width(32)) register_7 (.D(WriteData), .en(decoder_4_out3), .Q(register_7_q), .clk(Clk), .clr(Reset));
  Register #(.width(32)) register_8 (.D(WriteData), .en(decoder_5_out0), .Q(register_8_q), .clk(Clk), .clr(Reset));
  Register #(.width(32)) register_9 (.D(WriteData), .en(decoder_5_out1), .Q(register_9_q), .clk(Clk), .clr(Reset));
  Register #(.width(32)) register_10 (.D(WriteData), .en(decoder_5_out2), .Q(register_10_q), .clk(Clk), .clr(Reset));
  Register #(.width(32)) register_11 (.D(WriteData), .en(decoder_5_out3), .Q(register_11_q), .clk(Clk), .clr(Reset));
  Register #(.width(32)) register_12 (.D(WriteData), .en(decoder_6_out0), .Q(register_12_q), .clk(Clk), .clr(Reset));
  Register #(.width(32)) register_13 (.D(WriteData), .en(decoder_6_out1), .Q(register_13_q), .clk(Clk), .clr(Reset));
  Register #(.width(32)) register_14 (.D(WriteData), .en(decoder_6_out2), .Q(register_14_q), .clk(Clk), .clr(Reset));
  Register #(.width(32)) register_15 (.D(WriteData), .en(decoder_6_out3), .Q(register_15_q), .clk(Clk), .clr(Reset));
  // Probe on {32{1'b0}}
  // Probe on register_1_q
  // Probe on register_2_q
  // Probe on register_3_q
  // Probe on register_4_q
  // Probe on register_5_q
  // Probe on register_6_q
  // Probe on register_7_q
  // Probe on register_8_q
  // Probe on register_9_q
  // Probe on register_10_q
  // Probe on register_11_q
  // Probe on register_12_q
  // Probe on register_13_q
  // Probe on register_14_q
  // Probe on register_15_q
  // Probe on ReadReg1
  Multiplexer #(.select(2), .width(32), .enable("false")) multiplexer_1 (
    .in0({32{1'b0}}), .in1(register_1_q), .in2(register_2_q), .in3(register_3_q), .out(multiplexer_1_out),
    .sel(ReadReg1[1:0]));
  Multiplexer #(.select(2), .width(32), .enable("false")) multiplexer_2 (
    .in0(register_4_q), .in1(register_5_q), .in2(register_6_q), .in3(register_7_q), .out(multiplexer_2_out),
    .sel(ReadReg1[1:0]));
  Multiplexer #(.select(2), .width(32), .enable("false")) multiplexer_3 (
    .in0(register_8_q), .in1(register_9_q), .in2(register_10_q), .in3(register_11_q),
    .out(multiplexer_3_out), .sel(ReadReg1[1:0]));
  Multiplexer #(.select(2), .width(32), .enable("false")) multiplexer_4 (
    .in0(register_12_q), .in1(register_13_q), .in2(register_14_q), .in3(register_15_q),
    .out(multiplexer_4_out), .sel(ReadReg1[1:0]));
  // Probe on ReadReg2
  Multiplexer #(.select(2), .width(32), .enable("false")) multiplexer_5 (
    .in0({32{1'b0}}), .in1(register_1_q), .in2(register_2_q), .in3(register_3_q), .out(multiplexer_5_out),
    .sel(ReadReg2[1:0]));
  Multiplexer #(.select(2), .width(32), .enable("false")) multiplexer_6 (
    .in0(register_4_q), .in1(register_5_q), .in2(register_6_q), .in3(register_7_q), .out(multiplexer_6_out),
    .sel(ReadReg2[1:0]));
  Multiplexer #(.select(2), .width(32), .enable("false")) multiplexer_7 (
    .in0(register_8_q), .in1(register_9_q), .in2(register_10_q), .in3(register_11_q),
    .out(multiplexer_7_out), .sel(ReadReg2[1:0]));
  Multiplexer #(.select(2), .width(32), .enable("false")) multiplexer_8 (
    .in0(register_12_q), .in1(register_13_q), .in2(register_14_q), .in3(register_15_q),
    .out(multiplexer_8_out), .sel(ReadReg2[1:0]));
  Multiplexer #(.select(2), .width(32), .enable("false")) multiplexer_9 (
    .in0(multiplexer_5_out), .in1(multiplexer_6_out), .in2(multiplexer_7_out), .in3(multiplexer_8_out),
    .out(multiplexer_9_out), .sel(ReadReg2[3:2]));
  Multiplexer #(.select(2), .width(32), .enable("false")) multiplexer_10 (
    .in0(multiplexer_1_out), .in1(multiplexer_2_out), .in2(multiplexer_3_out), .in3(multiplexer_4_out),
    .out(multiplexer_10_out), .sel(ReadReg1[3:2]));
  Decoder #(.select(2), .disabled(0)) decoder_7 (
    .out0(decoder_7_out0), .out1(decoder_7_out1), .out2(decoder_7_out2), .out3(decoder_7_out3),
    .sel(WriteReg[3:2]), .en(decoder_1_out1));
  Decoder #(.select(2), .disabled(0)) decoder_8 (
    .out0(decoder_8_out0), .out1(decoder_8_out1), .out2(decoder_8_out2), .out3(decoder_8_out3),
    .sel(WriteReg[1:0]), .en(decoder_7_out0));
  Decoder #(.select(2), .disabled(0)) decoder_9 (
    .out0(decoder_9_out0), .out1(decoder_9_out1), .out2(decoder_9_out2), .out3(decoder_9_out3),
    .sel(WriteReg[1:0]), .en(decoder_7_out1));
  Decoder #(.select(2), .disabled(0)) decoder_10 (
    .out0(decoder_10_out0), .out1(decoder_10_out1), .out2(decoder_10_out2), .out3(decoder_10_out3),
    .sel(WriteReg[1:0]), .en(decoder_7_out2));
  Decoder #(.select(2), .disabled(0)) decoder_11 (
    .out0(decoder_11_out0), .out1(decoder_11_out1), .out2(decoder_11_out2), .out3(decoder_11_out3),
    .sel(WriteReg[1:0]), .en(decoder_7_out3));
  Register #(.width(32)) register_16 (.D(WriteData), .en(decoder_8_out0), .Q(register_16_q), .clk(Clk), .clr(Reset));
  Register #(.width(32)) register_17 (.D(WriteData), .en(decoder_8_out1), .Q(register_17_q), .clk(Clk), .clr(Reset));
  Register #(.width(32)) register_18 (.D(WriteData), .en(decoder_8_out2), .Q(register_18_q), .clk(Clk), .clr(Reset));
  Register #(.width(32)) register_19 (.D(WriteData), .en(decoder_8_out3), .Q(register_19_q), .clk(Clk), .clr(Reset));
  Register #(.width(32)) register_20 (.D(WriteData), .en(decoder_9_out0), .Q(register_20_q), .clk(Clk), .clr(Reset));
  Register #(.width(32)) register_21 (.D(WriteData), .en(decoder_9_out1), .Q(register_21_q), .clk(Clk), .clr(Reset));
  Register #(.width(32)) register_22 (.D(WriteData), .en(decoder_9_out2), .Q(register_22_q), .clk(Clk), .clr(Reset));
  Register #(.width(32)) register_23 (.D(WriteData), .en(decoder_9_out3), .Q(register_23_q), .clk(Clk), .clr(Reset));
  Register #(.width(32)) register_24 (.D(WriteData), .en(decoder_10_out0), .Q(register_24_q), .clk(Clk), .clr(Reset));
  Register #(.width(32)) register_25 (.D(WriteData), .en(decoder_10_out1), .Q(register_25_q), .clk(Clk), .clr(Reset));
  Register #(.width(32)) register_26 (.D(WriteData), .en(decoder_10_out2), .Q(register_26_q), .clk(Clk), .clr(Reset));
  Register #(.width(32)) register_27 (.D(WriteData), .en(decoder_10_out3), .Q(register_27_q), .clk(Clk), .clr(Reset));
  Register #(.width(32)) register_28 (.D(WriteData), .en(decoder_11_out0), .Q(register_28_q), .clk(Clk), .clr(Reset));
  Register #(.width(32)) register_29 (.D(WriteData), .en(decoder_11_out1), .Q(register_29_q), .clk(Clk), .clr(Reset));
  Register #(.width(32)) register_30 (.D(WriteData), .en(decoder_11_out2), .Q(register_30_q), .clk(Clk), .clr(Reset));
  Register #(.width(32)) register_31 (.D(WriteData), .en(decoder_11_out3), .Q(register_31_q), .clk(Clk), .clr(Reset));
  // Probe on register_16_q
  // Probe on register_17_q
  // Probe on register_18_q
  // Probe on register_19_q
  // Probe on register_20_q
  // Probe on register_21_q
  // Probe on register_22_q
  // Probe on register_23_q
  // Probe on register_24_q
  // Probe on register_25_q
  // Probe on register_26_q
  // Probe on register_27_q
  // Probe on register_28_q
  // Probe on register_29_q
  // Probe on register_30_q
  // Probe on register_31_q
  Multiplexer #(.width(32), .enable("false")) multiplexer_11 (
    .in0(multiplexer_10_out), .in1(multiplexer_21_out), .out(ReadData1), .sel(ReadReg1[4]));
  Multiplexer #(.width(32), .enable("false")) multiplexer_12 (
    .in0(multiplexer_9_out), .in1(multiplexer_22_out), .out(ReadData2), .sel(ReadReg2[4]));
  Multiplexer #(.select(2), .width(32), .enable("false")) multiplexer_13 (
    .in0(register_16_q), .in1(register_17_q), .in2(register_18_q), .in3(register_19_q),
    .out(multiplexer_13_out), .sel(ReadReg1[1:0]));
  Multiplexer #(.select(2), .width(32), .enable("false")) multiplexer_14 (
    .in0(register_20_q), .in1(register_21_q), .in2(register_22_q), .in3(register_23_q),
    .out(multiplexer_14_out), .sel(ReadReg1[1:0]));
  Multiplexer #(.select(2), .width(32), .enable("false")) multiplexer_15 (
    .in0(register_24_q), .in1(register_25_q), .in2(register_26_q), .in3(register_27_q),
    .out(multiplexer_15_out), .sel(ReadReg1[1:0]));
  Multiplexer #(.select(2), .width(32), .enable("false")) multiplexer_16 (
    .in0(register_28_q), .in1(register_29_q), .in2(register_30_q), .in3(register_31_q),
    .out(multiplexer_16_out), .sel(ReadReg1[1:0]));
  Multiplexer #(.select(2), .width(32), .enable("false")) multiplexer_17 (
    .in0(register_16_q), .in1(register_17_q), .in2(register_18_q), .in3(register_19_q),
    .out(multiplexer_17_out), .sel(ReadReg2[1:0]));
  Multiplexer #(.select(2), .width(32), .enable("false")) multiplexer_18 (
    .in0(register_20_q), .in1(register_21_q), .in2(register_22_q), .in3(register_23_q),
    .out(multiplexer_18_out), .sel(ReadReg2[1:0]));
  Multiplexer #(.select(2), .width(32), .enable("false")) multiplexer_19 (
    .in0(register_24_q), .in1(register_25_q), .in2(register_26_q), .in3(register_27_q),
    .out(multiplexer_19_out), .sel(ReadReg2[1:0]));
  Multiplexer #(.select(2), .width(32), .enable("false")) multiplexer_20 (
    .in0(register_28_q), .in1(register_29_q), .in2(register_30_q), .in3(register_31_q),
    .out(multiplexer_20_out), .sel(ReadReg2[1:0]));
  Multiplexer #(.select(2), .width(32), .enable("false")) multiplexer_21 (
    .in0(multiplexer_17_out), .in1(multiplexer_18_out), .in2(multiplexer_19_out), .in3(multiplexer_20_out),
    .out(multiplexer_21_out), .sel(ReadReg2[3:2]));
  Multiplexer #(.select(2), .width(32), .enable("false")) multiplexer_22 (
    .in0(multiplexer_13_out), .in1(multiplexer_14_out), .in2(multiplexer_15_out), .in3(multiplexer_16_out),
    .out(multiplexer_22_out), .sel(ReadReg1[3:2]));
endmodule

module Processor (
  output Overflow
);

  wire alu_1_branch, and_1_out, clock_1_out, control_unit_1_alurequired, control_unit_1_alusrc,
       control_unit_1_branch, control_unit_1_jump, control_unit_1_memread, control_unit_1_memtoreg,
       control_unit_1_memwrite, control_unit_1_r_type, control_unit_1_regdest, control_unit_1_regwrite,
       pull_resistor_1_node, Restart_Program_out, Zero_Reg_File_out;
  wire [1:0] control_unit_1_aluop;
  wire [3:0] alu_ctrl_1_alu_control;
  wire [4:0] multiplexer_1_out;
  wire [5:0] Opcode;
  wire [25:0] ram_1_data;
  wire [27:0] bit_extender_1_out, shifter_1_out;
  wire [31:0] adder_1_out, adder_2_out, alu_1_out_6, bit_extender_2_out, multiplexer_2_out,
       multiplexer_3_out, multiplexer_4_out, multiplexer_5_out, ram_2_data, register_1_q,
       register_file_1_readdata1, register_file_1_readdata2, shifter_2_out;

  Register #(.width(32)) register_1 (
    .D(multiplexer_4_out), .Q(register_1_q), .clk(clock_1_out), .clr(Restart_Program_out));  // open: en
  Button Zero_Reg_File (.out(Zero_Reg_File_out));
  Adder_part #(.width(32)) adder_1 (.a(register_1_q), .b(32'h4), .out(adder_1_out));  // open: cin, cout
  Button Restart_Program (.out(Restart_Program_out));
  Clock clock_1 (.out(clock_1_out));
  assign bit_extender_1_out = {{2{1'b0}}, ram_1_data};  // Bit_Extender bit_extender_1
  Pull_Resistor #(.pull(1)) pull_resistor_1 (.node(pull_resistor_1_node));
  Shifter #(.width(28)) shifter_1 (.in(bit_extender_1_out), .\dist (5'b00010), .out(shifter_1_out));
  RAM #(.addrWidth(24), .dataWidth(32)) ram_1 (
    .addr(register_1_q[25:2]), .data({Opcode, ram_1_data}), .ld(pull_resistor_1_node));  // open: sel, clk, clr
  Control_Unit control_unit_1 (
    .Jump(control_unit_1_jump), .ALURequired(control_unit_1_alurequired), .RegDest(control_unit_1_regdest),
    .Branch(control_unit_1_branch), .MemWrite(control_unit_1_memwrite), .MemRead(control_unit_1_memread),
    .MemToReg(control_unit_1_memtoreg), .RegWrite(control_unit_1_regwrite), .ALUSrc(control_unit_1_alusrc),
    .R_type(control_unit_1_r_type), .ALUOp(control_unit_1_aluop), .Opcode(Opcode));
  // Probe on ram_1_data[25:21]
  // Probe on ram_1_data[20:16]
  // Probe on multiplexer_1_out
  Multiplexer #(.width(5), .enable("false")) multiplexer_1 (
    .in0(ram_1_data[20:16]), .in1(ram_1_data[15:11]), .out(multiplexer_1_out), .sel(control_unit_1_regdest));
  assign bit_extender_2_out = {{16{1'b0}}, ram_1_data[15:0]};  // Bit_Extender bit_extender_2
  // Probe on multiplexer_5_out
  Register_file register_file_1 (
    .ReadReg1(ram_1_data[25:21]), .ReadReg2(ram_1_data[20:16]), .WriteReg(multiplexer_1_out),
    .RegWrite(control_unit_1_regwrite), .Reset(Zero_Reg_File_out), .ReadData1(register_file_1_readdata1),
    .ReadData2(register_file_1_readdata2), .WriteData(multiplexer_5_out), .Clk(clock_1_out));
  // Probe on register_file_1_readdata1
  // Probe on register_file_1_readdata2
  Multiplexer #(.width(32), .enable("false")) multiplexer_2 (
    .in0(register_file_1_readdata2), .in1(bit_extender_2_out), .out(multiplexer_2_out),
    .sel(control_unit_1_alusrc));
  ALU_CTRL alu_ctrl_1 (
    .OPCODE(Opcode), .Funct(ram_1_data[5:0]), .ALU_CONTROL(alu_ctrl_1_alu_control),
    .R_type(control_unit_1_r_type));
  Shifter #(.width(32)) shifter_2 (.in(bit_extender_2_out), .\dist (5'b00010), .out(shifter_2_out));
  and and_1 (and_1_out, control_unit_1_branch, alu_1_branch);
  Multiplexer #(.width(32), .enable("false")) multiplexer_3 (
    .in0(adder_1_out), .in1(adder_2_out), .out(multiplexer_3_out), .sel(and_1_out));
  Adder_part #(.width(32)) adder_2 (.a(adder_1_out), .b(shifter_2_out), .out(adder_2_out));  // open: cin, cout
  ALU alu_1 (
    .out_4(Overflow), .Branch(alu_1_branch), .out_6(alu_1_out_6), .in_2(register_file_1_readdata1),
    .in_3(multiplexer_2_out), .ALU_Control(alu_ctrl_1_alu_control));
  // Probe on alu_1_out_6[9:2]
  Multiplexer #(.width(32), .enable("false")) multiplexer_4 (
    .in0(multiplexer_3_out), .in1({adder_1_out[31:28], shifter_1_out}), .out(multiplexer_4_out),
    .sel(control_unit_1_jump));
  RAM #(.dataWidth(32), .bus("separate")) ram_2 (
    .addr(alu_1_out_6[9:2]), .din(register_file_1_readdata2), .data(ram_2_data),
    .str(control_unit_1_memwrite), .clk(clock_1_out), .ld(control_unit_1_memread));  // open: sel, clr
  Multiplexer #(.width(32), .enable("false")) multiplexer_5 (
    .in0(alu_1_out_6), .in1(ram_2_data), .out(multiplexer_5_out), .sel(control_unit_1_memtoreg));

  // Notes on the sheet:
  //   Immediate
  //   Funct
  //   Jump
  //   ALUOp
  //   RegDst
  //   Branch
  //   MemWrite
  //   MemRead
  //   MemToReg
  //   RegWrite
  //   ALUSrc
  //   R Type
  //   ALURequied
endmodule
